# Fritzing sketch limit-switches (saved by Fritzing 0.9.3b)
breadboards: 1

parts:
  Raspberry_Pi_1 = Raspberry Pi 3 [part_number=RPI-3-V1.2]
  Y-SW = Pushbutton [package=THT]
  Z-SW = Pushbutton [package=THT]
  X-SW = Pushbutton [package=THT]
  Y-SW_2 = Resistor [tolerance=±5% resistance=10k package="2512 [SMD]"]
  X-SW_2 = Resistor [tolerance=±5% resistance=10k package="0805 [SMD]"]
  Z-SW_2 = Resistor [tolerance=±5% resistance=10k package="0805 [SMD]"]
  GDS = Basic FET N-Channel [package="TO220 [THT]"]
  VCC1 = 4 x AAA Battery Mount
  MAGNET = Inductor [package="400 mil [THT]"]
  R4 = Resistor [tolerance=±5% resistance=1k package="0805 [SMD]"]

nets:
  N1: Raspberry_Pi_1.3v3, Y-SW_2.Pin_0, X-SW_2.Pin_0, Z-SW_2.Pin_0
  N2: Raspberry_Pi_1.GIPO17, Y-SW.leg1, Y-SW_2.Pin_1
  N3: Raspberry_Pi_1.GIPO27, X-SW.leg1, X-SW_2.Pin_1
  N4: Raspberry_Pi_1.GIPO22, R4.Pin_0
  N5: Raspberry_Pi_1.GND, Y-SW.leg0, Z-SW.leg0, X-SW.leg0, GDS.source, VCC1.-
  N6: Raspberry_Pi_1.GIPO23, Z-SW.leg1, Z-SW_2.Pin_1
  N7: GDS.gate, R4.Pin_1
  N8: GDS.drain, MAGNET.pin_1
  N9: VCC1.+, MAGNET.pin_0
